// Logisim project MIPS_CPU.circ as structural Verilog: 6 circuits, main circuit CO
module IA (
  input  [31:0] instruction,
  output [4:0] Rs,
  output [4:0] Rt,
  output [4:0] Rd,
  output [4:0] shamt,
  output [15:0] immi1,
  output [25:0] immi2
);

  assign Rs = instruction[25:21] | instruction[25:21];  // OR_Gate or_1, 5 bits wide
  assign Rt = instruction[20:16] | instruction[20:16];  // OR_Gate or_2, 5 bits wide

  assign immi1 = instruction[15:0];
  assign immi2 = instruction[25:0];
  assign Rd = instruction[15:11];
  assign shamt = instruction[10:6];
endmodule

module DM (
  input  [31:0] in_1,
  input  [23:0] address,
  input  store,
  input  enable,
  input  clock,
  input  clear,
  output [31:0] out_7
);

  RAM #(.addrWidth(24), .dataWidth(32), .bus("separate")) ram_1 (
    .addr(address), .din(in_1), .data(out_7), .str(store), .sel(enable), .clk(clock), .ld(1'b1), .clr(clear));
endmodule

module CO (
  input  [27:0] IN,
  output [1:0] R1_num,
  output [1:0] R2_num,
  output [1:0] W_num,
  output [2:0] Din,
  output [2:0] B,
  output WE,
  output [1:0] NPC,
  output [3:0] OP,
  output SYS,
  output BEQ,
  output READ,
  output WRITE,
  output BLTZ,
  output BNE
);

  or or_1 (OP[0], IN[0], IN[1], IN[2], IN[3], IN[4], IN[5], IN[7], IN[13], IN[14], IN[17], IN[18], IN[19], IN[24], IN[26], IN[27]);
  or or_2 (READ, IN[13], IN[26]);
  or or_3 (OP[1], IN[4], IN[5], IN[8], IN[9], IN[12], IN[15], IN[16], IN[17], IN[18], IN[19], IN[23], IN[27]);
  or or_4 (R1_num[0], IN[5], IN[6], IN[7], IN[8], IN[27]);
  or or_5 (W_num[0], IN[11], IN[1], IN[2], IN[13], IN[24], IN[25], IN[26], IN[18]);
  nor nor_1 (WE, IN[14], IN[15], IN[16], IN[20], IN[22], IN[23], IN[27]);
  or or_6 (OP[2], IN[0], IN[1], IN[2], IN[3], IN[4], IN[5], IN[9], IN[13], IN[14], IN[15], IN[16], IN[23], IN[26]);
  or or_7 (Din[0], IN[13], IN[25]);
  or or_8 (Din[1], IN[21], IN[25]);
  or or_9 (B[0], IN[1], IN[2], IN[5], IN[13], IN[14], IN[18], IN[24], IN[23]);
  or or_10 (B[1], IN[6], IN[7], IN[8], IN[23]);
  or or_11 (NPC[0], IN[20], IN[21]);
  or or_12 (OP[3], IN[10], IN[11], IN[12], IN[17], IN[18], IN[19], IN[24], IN[27]);
  or or_13 (B[2], IN[11], IN[26]);

  assign BEQ = IN[15];
  assign BLTZ = IN[27];
  assign BNE = IN[16];
  assign Din[2] = IN[26];
  assign NPC[1] = IN[22];
  assign R1_num[1] = IN[23];
  assign R2_num = {IN[23], IN[27]};
  assign SYS = IN[23];
  assign W_num[1] = IN[21];
  assign WRITE = IN[14];

  // Other names for the same wires on the sheet: Din2 = IN[26]; LH = IN[26]; Add = IN[0]; AddI = IN[1]; AddIU = IN[2];
  //   AddU = IN[3]; And = IN[4]; ANDI = IN[5]; SLL = IN[6]; SRA = IN[7]; SRL = IN[8]; SUB = IN[9]; OR = IN[10];
  //   ORI = IN[11]; NOR = IN[12]; LOADW = IN[13]; STOREW = IN[14]; SLT = IN[17]; SLTI = IN[18]; SLTU = IN[19];
  //   JUMP = IN[20]; XORI = IN[24]; LUI = IN[25]; JR = IN[22]; NPC1 = IN[22]; R1_0 = R1_num[0]; R2_0 = IN[27];
  //   R1_1 = IN[23]; R2_1 = IN[23]; W_0 = W_num[0]; JAL = IN[21]; W_1 = IN[21]
endmodule

module OP (
  input  [5:0] OP,
  input  [5:0] FUN,
  output [27:0] OP_2
);

  wire and_1_out, and_3_out, and_6_out, and_7_out, and_8_out, and_9_out, and_13_out, and_14_out, and_15_out,
       and_16_out, and_17_out, and_18_out, and_22_out, and_23_out, and_24_out, and_26_out, and_27_out,
       and_29_out, and_36_out, and_37_out, and_38_out, and_39_out, and_40_out, and_41_out, and_48_out,
       and_50_out;

  and and_1 (and_1_out, ~OP[0], ~OP[1], ~OP[2], ~OP[3], ~OP[4], ~OP[5]);  // AND_Gate
  and and_2 (OP_2[0], and_1_out, and_3_out);
  and and_3 (and_3_out, ~FUN[0], ~FUN[1], ~FUN[2], ~FUN[3], ~FUN[4], FUN[5]);  // AND_Gate
  and and_4 (OP_2[1], ~OP[0], ~OP[1], ~OP[2], OP[3], ~OP[4], ~OP[5]);  // AND_Gate
  and and_5 (OP_2[2], OP[0], ~OP[1], ~OP[2], OP[3], ~OP[4], ~OP[5]);  // AND_Gate
  and and_6 (and_6_out, ~OP[0], ~OP[1], ~OP[2], ~OP[3], ~OP[4], ~OP[5]);  // AND_Gate
  and and_7 (and_7_out, FUN[0], ~FUN[1], ~FUN[2], ~FUN[3], ~FUN[4], FUN[5]);  // AND_Gate
  and and_8 (and_8_out, ~OP[0], ~OP[1], ~OP[2], ~OP[3], ~OP[4], ~OP[5]);  // AND_Gate
  and and_9 (and_9_out, ~FUN[0], ~FUN[1], FUN[2], ~FUN[3], ~FUN[4], FUN[5]);  // AND_Gate
  and and_10 (OP_2[5], ~OP[0], ~OP[1], OP[2], OP[3], ~OP[4], ~OP[5]);  // AND_Gate
  and and_11 (OP_2[3], and_6_out, and_7_out);
  and and_12 (OP_2[4], and_8_out, and_9_out);
  and and_13 (and_13_out, ~OP[0], ~OP[1], ~OP[2], ~OP[3], ~OP[4], ~OP[5]);  // AND_Gate
  and and_14 (and_14_out, FUN[0], FUN[1], ~FUN[2], ~FUN[3], ~FUN[4], ~FUN[5]);  // AND_Gate
  and and_15 (and_15_out, ~OP[0], ~OP[1], ~OP[2], ~OP[3], ~OP[4], ~OP[5]);  // AND_Gate
  and and_16 (and_16_out, ~FUN[0], FUN[1], ~FUN[2], ~FUN[3], ~FUN[4], ~FUN[5]);  // AND_Gate
  and and_17 (and_17_out, ~OP[0], ~OP[1], ~OP[2], ~OP[3], ~OP[4], ~OP[5]);  // AND_Gate
  and and_18 (and_18_out, ~FUN[0], ~FUN[1], ~FUN[2], ~FUN[3], ~FUN[4], ~FUN[5]);  // AND_Gate
  and and_19 (OP_2[7], and_13_out, and_14_out);
  and and_20 (OP_2[8], and_15_out, and_16_out);
  and and_21 (OP_2[6], and_17_out, and_18_out);
  and and_22 (and_22_out, ~OP[0], ~OP[1], ~OP[2], ~OP[3], ~OP[4], ~OP[5]);  // AND_Gate
  and and_23 (and_23_out, ~FUN[0], FUN[1], ~FUN[2], ~FUN[3], ~FUN[4], FUN[5]);  // AND_Gate
  and and_24 (and_24_out, ~OP[0], ~OP[1], ~OP[2], ~OP[3], ~OP[4], ~OP[5]);  // AND_Gate
  and and_25 (OP_2[10], and_24_out, and_26_out);
  and and_26 (and_26_out, FUN[0], ~FUN[1], FUN[2], ~FUN[3], ~FUN[4], FUN[5]);  // AND_Gate
  and and_27 (and_27_out, ~OP[0], ~OP[1], ~OP[2], ~OP[3], ~OP[4], ~OP[5]);  // AND_Gate
  and and_28 (OP_2[12], and_27_out, and_29_out);
  and and_29 (and_29_out, FUN[0], FUN[1], FUN[2], ~FUN[3], ~FUN[4], FUN[5]);  // AND_Gate
  and and_30 (OP_2[9], and_22_out, and_23_out);
  and and_31 (OP_2[14], OP[0], OP[1], ~OP[2], OP[3], ~OP[4], OP[5]);  // AND_Gate
  and and_32 (OP_2[15], ~OP[0], ~OP[1], OP[2], ~OP[3], ~OP[4], ~OP[5]);  // AND_Gate
  and and_33 (OP_2[16], OP[0], ~OP[1], OP[2], ~OP[3], ~OP[4], ~OP[5]);  // AND_Gate
  and and_34 (OP_2[11], OP[0], ~OP[1], OP[2], OP[3], ~OP[4], ~OP[5]);  // AND_Gate
  and and_35 (OP_2[13], OP[0], OP[1], ~OP[2], ~OP[3], ~OP[4], OP[5]);  // AND_Gate
  and and_36 (and_36_out, ~OP[0], ~OP[1], ~OP[2], ~OP[3], ~OP[4], ~OP[5]);  // AND_Gate
  and and_37 (and_37_out, ~FUN[0], FUN[1], ~FUN[2], FUN[3], ~FUN[4], FUN[5]);  // AND_Gate
  and and_38 (and_38_out, ~OP[0], ~OP[1], ~OP[2], ~OP[3], ~OP[4], ~OP[5]);  // AND_Gate
  and and_39 (and_39_out, FUN[0], FUN[1], ~FUN[2], FUN[3], ~FUN[4], FUN[5]);  // AND_Gate
  and and_40 (and_40_out, ~OP[0], ~OP[1], ~OP[2], ~OP[3], ~OP[4], ~OP[5]);  // AND_Gate
  and and_41 (and_41_out, ~FUN[0], ~FUN[1], ~FUN[2], FUN[3], ~FUN[4], ~FUN[5]);  // AND_Gate
  and and_42 (OP_2[17], and_36_out, and_37_out);
  and and_43 (OP_2[19], and_38_out, and_39_out);
  and and_44 (OP_2[22], and_40_out, and_41_out);
  and and_45 (OP_2[18], ~OP[0], OP[1], ~OP[2], OP[3], ~OP[4], ~OP[5]);  // AND_Gate
  and and_46 (OP_2[20], ~OP[0], OP[1], ~OP[2], ~OP[3], ~OP[4], ~OP[5]);  // AND_Gate
  and and_47 (OP_2[21], OP[0], OP[1], ~OP[2], ~OP[3], ~OP[4], ~OP[5]);  // AND_Gate
  and and_48 (and_48_out, ~OP[0], ~OP[1], ~OP[2], ~OP[3], ~OP[4], ~OP[5]);  // AND_Gate
  and and_49 (OP_2[23], and_48_out, and_50_out);
  and and_50 (and_50_out, ~FUN[0], ~FUN[1], FUN[2], FUN[3], ~FUN[4], ~FUN[5]);  // AND_Gate
  and and_51 (OP_2[24], ~OP[0], OP[1], OP[2], OP[3], ~OP[4], ~OP[5]);  // AND_Gate
  and and_52 (OP_2[25], OP[0], OP[1], OP[2], OP[3], ~OP[4], ~OP[5]);  // AND_Gate
  and and_53 (OP_2[26], OP[0], ~OP[1], ~OP[2], ~OP[3], ~OP[4], OP[5]);  // AND_Gate
  and and_54 (OP_2[27], OP[0], ~OP[1], ~OP[2], ~OP[3], ~OP[4], ~OP[5]);  // AND_Gate

  // Other names for the same wires on the sheet: Add = OP_2[0]; AddI = OP_2[1]; AddIU = OP_2[2]; AddU = OP_2[3];
  //   And = OP_2[4]; ANDI = OP_2[5]; SLL = OP_2[6]; SRA = OP_2[7]; SRL = OP_2[8]; SUB = OP_2[9]; OR = OP_2[10];
  //   ORI = OP_2[11]; NOR = OP_2[12]; LOADW = OP_2[13]; STOREW = OP_2[14]; BEQ = OP_2[15]; BNE = OP_2[16];
  //   SLT = OP_2[17]; SLTI = OP_2[18]; SLTU = OP_2[19]; JUMP = OP_2[20]; JAL = OP_2[21]; JR = OP_2[22];
  //   SYS = OP_2[23]; XORI = OP_2[24]; LUI = OP_2[25]; LH = OP_2[26]; BLTZ = OP_2[27]

  // Notes on the sheet:
  //   AddI(1000)
  //   AddIU(1001)
  //   Add(100000)
  //   AddU(100001)
  //   And(100100)
  //   ANDI(1100)
  //   SRA(11)
  //   SRL(10)
  //   SLL(0)
  //   SUB(100010)
  //   OR(100101)
  //   NOR(100111)
  //   ORI(1101)
  //   LOADW(100011)
  //   STOREW(101011)
  //   BEQ(100)
  //   BNE(101)
  //   SLT(101010)
  //   SLTU(101011)
  //   JR(1000)
  //   SLTI(1010)
  //   JUMP(10)
  //   JAL(11)
  //   SYS(1100)
  //   XORI(1110)
  //   LUI(1111)
  //   LH(100001)
  //   BLTZ(1)
endmodule

module MAIN (
  input  enable
);

  wire alu_1_p4, and_1_out, and_2_out, and_4_out, and_6_out, and_7_out, and_8_out, BEQ, BLTZ, BNE, CLEAR,
       CLK, co_1_read, co_1_write, COUNT, HALT, NPCC, or_1_out, or_2_out, OUTC, SYS, WE;
  wire [1:0] NPC, R1_num, R2_num, W_num;
  wire [2:0] B, Din;
  wire [3:0] OP;
  wire [4:0] IA_rd, IA_rs, IA_rt, IA_shamt, multiplexer_4_out, multiplexer_5_out, multiplexer_6_out;
  wire [9:0] adder_1_out, adder_2_out, adder_3_out, bit_extender_1_out, bit_extender_2_out,
       bit_extender_3_out, multiplexer_1_out, multiplexer_2_out, PC_q, shifter_3_out;
  wire [15:0] bit_extender_8_out, bit_extender_10_out, IA_immi1, shifter_2_out, \总周期数 , \无条件分支指令数 ,
       \有条件分支成功跳转 , \有条件分支指令数 ;
  wire [25:0] IA_immi2, shifter_1_out;
  wire [27:0] OP_op_2;
  wire [31:0] alu_1_p2, alu_1_p5, bit_extender_4_out, bit_extender_5_out, bit_extender_6_out,
       bit_extender_7_out, bit_extender_9_out, multiplexer_3_out, OUTPUT, ram_1_data, registerfile_1_p7,
       rom_1_data, shifter_4_out, shifter_5_out, SyscallOut;

  Button \u_总复位  (.out(CLEAR));
  Clock u_clk (.out(CLK));
  Adder #(.width(10)) adder_1 (.a(10'h4), .b(bit_extender_3_out), .out(adder_1_out));  // open: cin, cout
  Hex_Digit_Display hex_digit_display_1 (.value(SyscallOut[31:28]));  // open: dp
  Hex_Digit_Display hex_digit_display_2 (.value(SyscallOut[27:24]));  // open: dp
  Adder #(.width(10)) adder_2 (.a(PC_q), .b(multiplexer_1_out), .out(adder_2_out));  // open: cin, cout
  Multiplexer #(.width(10)) multiplexer_1 (
    .in0(10'h4), .in1(adder_1_out), .out(multiplexer_1_out), .sel(NPCC), .en(enable));
  Shifter #(.width(26)) shifter_1 (.in(IA_immi2), .\dist (5'b00010), .out(shifter_1_out));
  Register #(.width(32)) register_1 (.D(OUTPUT), .en(OUTC), .Q(SyscallOut), .clk(CLK), .clr(CLEAR));
  and and_1 (and_1_out, ~NPC[1], NPC[0]);  // AND_Gate
  Hex_Digit_Display hex_digit_display_3 (.value(SyscallOut[23:20]));  // open: dp
  Hex_Digit_Display hex_digit_display_4 (.value(SyscallOut[19:16]));  // open: dp
  Bit_Extender #(.in_width(32), .out_width(10)) bit_extender_1 (.in(registerfile_1_p7), .out(bit_extender_1_out));
  Bit_Extender #(.in_width(26), .out_width(10)) bit_extender_2 (.in(shifter_1_out), .out(bit_extender_2_out));
  or or_1 (or_1_out, and_1_out, and_2_out);
  and and_2 (and_2_out, NPC[1], ~NPC[0]);  // AND_Gate
  Hex_Digit_Display hex_digit_display_5 (.value(SyscallOut[11:8]));  // open: dp
  Hex_Digit_Display hex_digit_display_6 (.value(SyscallOut[15:12]));  // open: dp
  Multiplexer #(.select(2), .width(10)) multiplexer_2 (
    .in0(adder_2_out), .in1(bit_extender_2_out), .in2(bit_extender_1_out), .in3({10{1'b0}}),
    .out(multiplexer_2_out), .sel(NPC), .en(enable));
  Register #(.width(10)) PC (.D(multiplexer_2_out), .en(COUNT), .Q(PC_q), .clk(CLK), .clr(CLEAR));
  Shifter #(.width(16)) shifter_2 (.in(IA_immi1), .\dist (4'b0010), .out(shifter_2_out));
  COUNT count_1 (.ENABLE(COUNT), .CLK(CLK), .CLEAR(CLEAR), .OUT(\总周期数 ));
  COUNT count_2 (.ENABLE(or_1_out), .CLK(CLK), .CLEAR(CLEAR), .OUT(\无条件分支指令数 ));
  or or_2 (or_2_out, BLTZ, BEQ, BNE);
  Hex_Digit_Display hex_digit_display_7 (.value(SyscallOut[3:0]));  // open: dp
  Hex_Digit_Display hex_digit_display_8 (.value(SyscallOut[7:4]));  // open: dp
  Bit_Extender #(.in_width(16), .out_width(10)) bit_extender_3 (.in(shifter_2_out), .out(bit_extender_3_out));
  COUNT count_3 (.ENABLE(or_2_out), .CLK(CLK), .CLEAR(CLEAR), .OUT(\有条件分支指令数 ));
  Adder #(.width(10)) adder_3 (.a(PC_q), .b(10'h4), .out(adder_3_out));  // open: cin, cout
  assign bit_extender_4_out = {{22{1'b0}}, adder_3_out};  // Bit_Extender bit_extender_4
  Shifter #(.width(10), .shift("lr")) shifter_3 (.in(PC_q), .\dist (4'b0010), .out(shifter_3_out));
  and and_3 (COUNT, enable, ~HALT);  // AND_Gate
  COUNT count_4 (.ENABLE(NPCC), .CLK(CLK), .CLEAR(CLEAR), .OUT(\有条件分支成功跳转 ));
  // Probe on \总周期数 
  // Probe on \无条件分支指令数 
  // Probe on \有条件分支指令数 
  // Probe on \有条件分支成功跳转 
  ROM #(.addrWidth(10), .dataWidth(32)) rom_1 (.addr(shifter_3_out), .data(rom_1_data), .sel(enable));
  CO co_1 (
    .IN(OP_op_2), .R1_num(R1_num), .R2_num(R2_num), .W_num(W_num), .Din(Din), .B(B), .NPC(NPC), .OP(OP),
    .WE(WE), .READ(co_1_read), .WRITE(co_1_write), .SYS(SYS), .BEQ(BEQ), .BLTZ(BLTZ), .BNE(BNE));
  OP u_OP (.OP(rom_1_data[31:26]), .FUN(rom_1_data[5:0]), .OP_2(OP_op_2));
  IA IA (
    .instruction(rom_1_data), .Rs(IA_rs), .Rt(IA_rt), .Rd(IA_rd), .shamt(IA_shamt), .immi1(IA_immi1),
    .immi2(IA_immi2));
  assign bit_extender_5_out = {{16{IA_immi1[15]}}, IA_immi1};  // Bit_Extender bit_extender_5
  assign bit_extender_6_out = {{27{1'b0}}, IA_shamt};  // Bit_Extender bit_extender_6
  assign bit_extender_7_out = {{16{1'b0}}, IA_immi1};  // Bit_Extender bit_extender_7
  Bit_Extender #(.in_width(32)) bit_extender_8 (.in(ram_1_data), .out(bit_extender_8_out));
  Multiplexer #(.select(3), .width(32)) multiplexer_3 (
    .in0(alu_1_p5), .in1(ram_1_data), .in2(bit_extender_4_out), .in3(shifter_4_out),
    .in4(bit_extender_9_out), .in5({32{1'b0}}), .in6({32{1'b0}}), .in7({32{1'b0}}), .out(multiplexer_3_out),
    .sel(Din), .en(enable));
  Shifter #(.width(32)) shifter_4 (.in(bit_extender_5_out), .\dist (5'b10000), .out(shifter_4_out));
  Multiplexer #(.select(2), .width(5)) multiplexer_4 (
    .in0(IA_rs), .in1(IA_rt), .in2(5'b00010), .in3({5{1'b0}}), .out(multiplexer_4_out), .sel(R1_num),
    .en(enable));
  Multiplexer #(.select(2), .width(5)) multiplexer_5 (
    .in0(IA_rt), .in1({5{1'b0}}), .in2(5'b00100), .in3({5{1'b0}}), .out(multiplexer_5_out), .sel(R2_num),
    .en(enable));
  assign bit_extender_9_out = {{16{bit_extender_8_out[15]}}, bit_extender_8_out};  // Bit_Extender bit_extender_9
  Multiplexer #(.select(2), .width(5)) multiplexer_6 (
    .in0(IA_rd), .in1(IA_rt), .in2({5{1'b1}}), .in3({5{1'b0}}), .out(multiplexer_6_out), .sel(W_num),
    .en(enable));
  // RegisterFile registerfile_1: pin names not known; wires that end beside it: multiplexer_3_out, CLK, WE, multiplexer_6_out, multiplexer_4_out, multiplexer_5_out, registerfile_1_p7, OUTPUT
  // ALU alu_1: pin names not known; wires that end beside it: registerfile_1_p7, alu_1_p2, OP, alu_1_p4, alu_1_p5
  Multiplexer #(.select(3), .width(32)) multiplexer_7 (
    .in0(OUTPUT), .in1(bit_extender_5_out), .in2(bit_extender_6_out), .in3(32'ha), .in4(bit_extender_7_out),
    .in5({32{1'b0}}), .in6({32{1'b0}}), .in7({32{1'b0}}), .out(alu_1_p2), .sel(B), .en(enable));
  and and_4 (and_4_out, SYS, alu_1_p4);
  and and_5 (OUTC, SYS, ~alu_1_p4);  // AND_Gate
  and and_6 (and_6_out, BLTZ, alu_1_p5[0]);
  and and_7 (and_7_out, BNE, ~alu_1_p4);  // AND_Gate
  and and_8 (and_8_out, BEQ, alu_1_p4);
  Bit_Extender #(.in_width(32)) bit_extender_10 (.in(shifter_5_out), .out(bit_extender_10_out));
  Shifter #(.width(32), .shift("lr")) shifter_5 (.in(alu_1_p5), .\dist (5'b00010), .out(shifter_5_out));
  D_Flip_Flop d_ff_1 (.clk(CLK), .D(and_4_out), .Q(HALT), .en(COUNT), .reset(CLEAR));  // open: Qn, preset
  or or_3 (NPCC, and_6_out, and_7_out, and_8_out);
  RAM #(.addrWidth(16), .dataWidth(32), .bus("separate")) ram_1 (
    .addr(bit_extender_10_out), .din(OUTPUT), .data(ram_1_data), .str(co_1_write), .sel(enable), .clk(CLK),
    .ld(co_1_read), .clr(CLEAR));

  // Other names for the same wires on the sheet: RST = CLEAR

  // Notes on the sheet:
  //   NPC_CON
  //   数码管输出应该用寄存器锁存，否则显示数据只能一闪而过
  //   可以通过项目增加Logisim库的方式将前几次实验完成的电路作为子电路引入到本电路中使用
  //   NPC
  //   数码管输出
  //   总复位信号应将除ROM以外所有存储组件全部清零
  //   IM
  //   contents of rom_1 (hex, n*v repeats v):
  //   20110001 8100005 20110001 20120002 20130003 8100009 20110001 20120002 20130003 810000d 20110001
  //   20120002 20130003 8100011 20110001 20120002 20130003 c1000b8 20100001 20110001 118fc0 112020
  //   20020022 c 118882 12200001 8100015 112020 20020022 c 20110001 118880 112020 20020022 c 12200001
  //   810001f 20110001 118fc0 112020 20020022 c 1188c3 112020 20020022 c 118903 112020 20020022 c 118903
  //   112020 20020022 c 118903 112020 20020022 c 118903 112020 20020022 c 118903 112020 20020022 c 118903
  //   112020 20020022 c 118903 112020 20020022 c 20100001 109fc0 139fc3 8021 2012000c 24160003 26100001
  //   3210000f 20080008 20090001 139900 2709825 132020 20020022 c 1094022 1500fff9 22100001 2018000f
  //   2188024 108700 20080008 20090001 139902 2709825 132021 20020022 c 1094022 1500fff9 108702 2c9b022
  //   12c00001 8100050 4020 1084027 84400 3508ffff 82021 20020022 c 2010ffff 20110000 ae300000 22100001
  //   22310004 ae300000 22100001 22310004 ae300000 22100001 22310004 ae300000 22100001 22310004 ae300000
  //   22100001 22310004 ae300000 22100001 22310004 ae300000 22100001 22310004 ae300000 22100001 22310004
  //   ae300000 22100001 22310004 ae300000 22100001 22310004 ae300000 22100001 22310004 ae300000 22100001
  //   22310004 ae300000 22100001 22310004 ae300000 22100001 22310004 ae300000 22100001 22310004 ae300000
  //   22100001 22310004 22100001 8020 2011003c 8e130000 8e340000 274402a 11000002 ae330000 ae140000
  //   2231fffc 1611fff8 102020 20020022 c 22100004 2011003c 1611fff2 2002000a c 20100000 22100001 102020
  //   20020022 c 22100002 102020 20020022 c 22100003 102020 20020022 c 22100004 102020 20020022 c 22100005
  //   102020 20020022 c 22100006 102020 20020022 c 22100007 102020 20020022 c 22100008 102020 20020022
  //   20020022 c 3e00008
endmodule

module COUNT (
  input  ENABLE,
  input  CLK,
  input  CLEAR,
  output [15:0] OUT
);

  wire [15:0] adder_1_out;

  Adder #(.width(16)) adder_1 (.a(OUT), .b(16'h1), .out(adder_1_out));  // open: cin, cout
  Register #(.width(16)) register_1 (.D(adder_1_out), .en(ENABLE), .Q(OUT), .clk(CLK), .clr(CLEAR));
endmodule
